// Logisim project ALU.circ as structural Verilog: 4 circuits, main circuit ALU
module ALU (
  input  [3:0] sel,
  input  [31:0] dataB,
  input  [31:0] dataA,
  output [31:0] dataD
);

  wire [31:0] adder_1_out, and_1_out, or_1_out, shifter_1_out, shifter_2_out, shifter_3_out, slt_1_p3,
       sltu_1_outd, subtractor_1_out, xor_1_out;

  Adder #(.width(32)) adder_1 (.a(dataA), .b(dataB), .out(adder_1_out));  // open: cin, cout
  Shifter #(.width(32)) shifter_1 (.in(dataA), .\dist (dataB[4:0]), .out(shifter_1_out));
  // slt slt_1: pin names not known; wires that end beside it: dataA, dataB, slt_1_p3
  sltu sltu_1 (.InpA(dataA), .inpB(dataB), .outD(sltu_1_outd));
  assign xor_1_out = dataA ^ dataB;  // XOR_Gate xor_1, 32 bits wide
  Shifter #(.shift("lr"), .width(32)) shifter_2 (.in(dataA), .\dist (dataB[4:0]), .out(shifter_2_out));
  assign or_1_out = dataA | dataB;  // OR_Gate or_1, 32 bits wide
  assign and_1_out = dataA & dataB;  // AND_Gate and_1, 32 bits wide
  Subtractor #(.width(32)) subtractor_1 (.a(dataA), .b(dataB), .out(subtractor_1_out));  // open: bin, bout
  Shifter #(.shift("ar"), .width(32)) shifter_3 (.in(dataA), .\dist (dataB[4:0]), .out(shifter_3_out));
  Multiplexer #(.select(4), .width(32)) multiplexer_1 (
    .in0(adder_1_out), .in1(shifter_1_out), .in2(slt_1_p3), .in3(sltu_1_outd), .in4(xor_1_out),
    .in5(shifter_2_out), .in6(or_1_out), .in7(and_1_out), .in8(subtractor_1_out), .in13(shifter_3_out),
    .out(dataD), .sel(sel));  // open: in9, in10, in11, in12, in14, in15
endmodule

module slt (
  input  [31:0] InpA,
  input  [31:0] inpB,
  output [31:0] outD
);

  wire comparator_1_lt;

  Comparator #(.width(32)) comparator_1 (.a(InpA), .b(inpB), .lt(comparator_1_lt));  // open: gt, eq
  assign outD = {{31{1'b0}}, comparator_1_lt};  // Bit_Extender bit_extender_1
endmodule

module sltu (
  input  [31:0] InpA,
  input  [31:0] inpB,
  output [31:0] outD
);

  wire comparator_1_lt;

  Comparator #(.mode("unsigned"), .width(32)) comparator_1 (.a(InpA), .b(inpB), .lt(comparator_1_lt));  // open: gt, eq
  assign outD = {{31{1'b0}}, comparator_1_lt};  // Bit_Extender bit_extender_1
endmodule

module test (
  input  [3:0] in_1,
  input  [31:0] in_2,
  input  [31:0] in_3,
  output [31:0] out_4
);

  ALU alu_1 (.sel(in_1), .dataB(in_2), .dataA(in_3), .dataD(out_4));
endmodule
