// Logisim project BranchingModule.circ as structural Verilog: 1 circuit, main circuit branchDetector
module branchDetector (
  input  [31:0] dataA,
  input  [31:0] dataB,
  input  [2:0] branchSelect,
  output takeBranch
);

  wire comparator_1_eq, comparator_1_lt, comparator_2_eq, comparator_2_lt, not_1_out, not_2_out, not_3_out;

  Comparator #(.width(32)) comparator_1 (.a(dataA), .b(dataB), .eq(comparator_1_eq), .lt(comparator_1_lt));  // open: gt
  Comparator #(.mode("unsigned"), .width(32)) comparator_2 (
    .a(dataA), .b(dataB), .eq(comparator_2_eq), .lt(comparator_2_lt));  // open: gt
  not not_1 (not_1_out, comparator_1_lt);
  not not_2 (not_2_out, comparator_2_eq);
  not not_3 (not_3_out, comparator_2_lt);
  Multiplexer #(.select(3)) multiplexer_1 (
    .in0(1'b0), .in1(comparator_1_eq), .in2(comparator_1_lt), .in3(not_1_out), .in4(1'b1), .in5(not_2_out),
    .in6(comparator_2_lt), .in7(not_3_out), .out(takeBranch), .sel(branchSelect));

  // Notes on the sheet:
  //   Branch Select
  //   000
  //   001
  //   010
  //   011
  //   100
  //   101
  //   110
  //   111
  //   Branch Select Truth table
  //   blt
  //   Output
  //   dont branch
  //   beq
  //   bge
  //   always branch
  //   bne
  //   bltu
  //   bgeu
endmodule
