// Logisim project Computor.circ as structural Verilog: 2 circuits, main circuit main
module main (
  input  [31:0] instruction,
  output [31:0] result
);

  wire alu_1_p4, alu_1_p6, alu_1_p8, clock_1_out, decodemodule_1_p3, decodemodule_1_p5, decodemodule_1_p7;
  wire [4:0] decodemodule_1_p4, decodemodule_1_p6, decodemodule_1_p8;
  wire [31:0] decodemodule_1_p1, registerfile32_1_rs1;

  Clock clock_1 (.out(clock_1_out));
  // DecodeModule decodemodule_1: pin names not known; wires that end beside it: decodemodule_1_p1, instruction, decodemodule_1_p3, decodemodule_1_p4, decodemodule_1_p5, decodemodule_1_p6, decodemodule_1_p7, decodemodule_1_p8
  RegisterFile32 registerfile32_1 (
    .load(decodemodule_1_p5), .rsi1(decodemodule_1_p6), .rsi2(decodemodule_1_p8), .rdi(decodemodule_1_p4),
    .rd(result), .Clock(clock_1_out), .rs1(registerfile32_1_rs1), .rs2(decodemodule_1_p1));
  // ALU alu_1: pin names not known; wires that end beside it: decodemodule_1_p7, registerfile32_1_rs1, decodemodule_1_p3, alu_1_p4, alu_1_p4, alu_1_p6, alu_1_p6, alu_1_p8, alu_1_p8, result
  memoryModule memorymodule_1 (
    .clock(clock_1_out), .data(result), .address(registerfile32_1_rs1), .memOut(result));  // open: funct_3
endmodule

module v2 (
  input  [31:0] instruction,
  input  in_2,
  output [31:0] data
);

  wire alu_1_p2, alu_1_p3, clock_1_out, decodemodule_1_p2, decodemodule_1_p3, decodemodule_1_p4,
       decodemodule_1_p5, decodemodule_1_p6, decodemodule_1_p7, decodemodule_1_p8, immediategenerator_1_p3,
       registerfile32_1_p3, registerfile32_1_p8;
  wire [31:0] alu_1_p4, memorymodule_1_p5;

  Clock clock_1 (.out(clock_1_out));
  // DecodeModule decodemodule_1: pin names not known; wires that end beside it: instruction, decodemodule_1_p2, decodemodule_1_p3, decodemodule_1_p4, decodemodule_1_p5, decodemodule_1_p6, decodemodule_1_p7, decodemodule_1_p8
  // ALU alu_1: pin names not known; wires that end beside it: decodemodule_1_p4, alu_1_p2, alu_1_p3, alu_1_p4
  Multiplexer #(.width(32)) multiplexer_1 (.in0(alu_1_p4), .in1(memorymodule_1_p5), .out(data), .sel(in_2));
  // RegisterFile32 registerfile32_1: pin names not known; wires that end beside it: decodemodule_1_p2, decodemodule_1_p8, registerfile32_1_p3, decodemodule_1_p7, data, clock_1_out, alu_1_p2, registerfile32_1_p8
  // ImmediateGenerator immediategenerator_1: pin names not known; wires that end beside it: instruction, decodemodule_1_p5, immediategenerator_1_p3
  // memoryModule memorymodule_1: pin names not known; wires that end beside it: clock_1_out, alu_1_p2, alu_1_p4, decodemodule_1_p6, memorymodule_1_p5
  // ImmediateSelector immediateselector_1: pin names not known; wires that end beside it: immediategenerator_1_p3, registerfile32_1_p8, decodemodule_1_p3, alu_1_p3
  // Probe on memorymodule_1_p5
endmodule
