// Logisim project ImmediateGenerator.circ as structural Verilog: 1 circuit, main circuit ImmediateGenerator
module ImmediateGenerator (
  input  [31:0] instruction,
  input  [2:0] sel,
  output [31:0] immediate_31_0
);

  wire [3:0] b_splitter_1_immediate_4_1;
  wire [4:0] s_splitter_1_immediate_4_0;
  wire [5:0] b_splitter_1_immediate_10_5;
  wire [6:0] s_splitter_1_immediate_11_5;
  wire [7:0] j_splitter_1_immediate_19_12;
  wire [9:0] j_splitter_1_immediate_10_1;
  wire [11:0] i_splitter_1_immediate;
  wire [12:11] b_splitter_1_immediate_11;
  wire [19:0] u_splitter_1_immediate;
  wire [20:11] j_splitter_1_immediate_11;
  wire [31:0] bit_extender_1_out, bit_extender_2_out, bit_extender_3_out, bit_extender_4_out;

  I_Splitter i_splitter_1 (
    .instruction(instruction), .immediate(i_splitter_1_immediate));  // open: opcode, rd_i, funct_3, rs1_i
  S_Splitter s_splitter_1 (
    .instruction(instruction), .immediate_4_0(s_splitter_1_immediate_4_0),
    .immediate_11_5(s_splitter_1_immediate_11_5));  // open: opcode, funct_3, rs1_i, rs2_i
  B_Splitter b_splitter_1 (
    .instruction(instruction), .immediate_11(b_splitter_1_immediate_11[11]),
    .immediate_4_1(b_splitter_1_immediate_4_1), .immediate_10_5(b_splitter_1_immediate_10_5),
    .immediate_12(b_splitter_1_immediate_11[12]));  // open: opcode, funct_3, rs1_i, rs2_i
  J_Splitter j_splitter_1 (
    .instruction(instruction), .immediate_19_12(j_splitter_1_immediate_19_12),
    .immediate_11(j_splitter_1_immediate_11[11]), .immediate_10_1(j_splitter_1_immediate_10_1),
    .immediate_12(j_splitter_1_immediate_11[20]));  // open: opcode, rd_i
  U_Splitter u_splitter_1 (.instruction(instruction), .immediate(u_splitter_1_immediate));  // open: opcode, rd_i
  assign bit_extender_1_out = {{20{i_splitter_1_immediate[11]}}, i_splitter_1_immediate};  // Bit_Extender bit_extender_1
  assign bit_extender_2_out = {{20{s_splitter_1_immediate_11_5[6]}}, {s_splitter_1_immediate_11_5, s_splitter_1_immediate_4_0}};  // Bit_Extender bit_extender_2
  assign bit_extender_3_out = {{19{b_splitter_1_immediate_11[12]}}, {b_splitter_1_immediate_11, b_splitter_1_immediate_10_5, b_splitter_1_immediate_4_1, 1'b0}};  // Bit_Extender bit_extender_3
  assign bit_extender_4_out = {{11{j_splitter_1_immediate_11[20]}}, {j_splitter_1_immediate_11[20], j_splitter_1_immediate_19_12, j_splitter_1_immediate_11[11], j_splitter_1_immediate_10_1, 1'b0}};  // Bit_Extender bit_extender_4
  Multiplexer #(.select(3), .width(32)) multiplexer_1 (
    .in0(bit_extender_1_out), .in1(bit_extender_2_out), .in2(bit_extender_3_out), .in3(bit_extender_4_out),
    .in4({u_splitter_1_immediate, {12{1'b0}}}), .out(immediate_31_0), .sel(sel));  // open: in5, in6, in7
endmodule
