// Logisim project InstructionFetchModule.circ as structural Verilog: 2 circuits, main circuit main
module main (
  input  in_1,
  input  in_2
);

  wire clock_1_out;
  wire [14:0] dipswitch_3_sw15, programcounter_1_outp;
  wire [31:0] dipswitch_1_sw32, dipswitch_2_sw32, programcounter_1_outp_2, ram128kb_1_p6;

  DipSwitch #(.number(32)) dipswitch_1 (
    .sw1(dipswitch_1_sw32[31]), .sw2(dipswitch_1_sw32[30]), .sw3(dipswitch_1_sw32[29]),
    .sw4(dipswitch_1_sw32[28]), .sw5(dipswitch_1_sw32[27]), .sw6(dipswitch_1_sw32[26]),
    .sw7(dipswitch_1_sw32[25]), .sw8(dipswitch_1_sw32[24]), .sw9(dipswitch_1_sw32[23]),
    .sw10(dipswitch_1_sw32[22]), .sw11(dipswitch_1_sw32[21]), .sw12(dipswitch_1_sw32[20]),
    .sw13(dipswitch_1_sw32[19]), .sw14(dipswitch_1_sw32[18]), .sw15(dipswitch_1_sw32[17]),
    .sw16(dipswitch_1_sw32[16]), .sw17(dipswitch_1_sw32[15]), .sw18(dipswitch_1_sw32[14]),
    .sw19(dipswitch_1_sw32[13]), .sw20(dipswitch_1_sw32[12]), .sw21(dipswitch_1_sw32[11]),
    .sw22(dipswitch_1_sw32[10]), .sw23(dipswitch_1_sw32[9]), .sw24(dipswitch_1_sw32[8]),
    .sw25(dipswitch_1_sw32[7]), .sw26(dipswitch_1_sw32[6]), .sw27(dipswitch_1_sw32[5]),
    .sw28(dipswitch_1_sw32[4]), .sw29(dipswitch_1_sw32[3]), .sw30(dipswitch_1_sw32[2]),
    .sw31(dipswitch_1_sw32[1]), .sw32(dipswitch_1_sw32[0]));
  DipSwitch #(.number(32)) dipswitch_2 (
    .sw1(dipswitch_2_sw32[31]), .sw2(dipswitch_2_sw32[30]), .sw3(dipswitch_2_sw32[29]),
    .sw4(dipswitch_2_sw32[28]), .sw5(dipswitch_2_sw32[27]), .sw6(dipswitch_2_sw32[26]),
    .sw7(dipswitch_2_sw32[25]), .sw8(dipswitch_2_sw32[24]), .sw9(dipswitch_2_sw32[23]),
    .sw10(dipswitch_2_sw32[22]), .sw11(dipswitch_2_sw32[21]), .sw12(dipswitch_2_sw32[20]),
    .sw13(dipswitch_2_sw32[19]), .sw14(dipswitch_2_sw32[18]), .sw15(dipswitch_2_sw32[17]),
    .sw16(dipswitch_2_sw32[16]), .sw17(dipswitch_2_sw32[15]), .sw18(dipswitch_2_sw32[14]),
    .sw19(dipswitch_2_sw32[13]), .sw20(dipswitch_2_sw32[12]), .sw21(dipswitch_2_sw32[11]),
    .sw22(dipswitch_2_sw32[10]), .sw23(dipswitch_2_sw32[9]), .sw24(dipswitch_2_sw32[8]),
    .sw25(dipswitch_2_sw32[7]), .sw26(dipswitch_2_sw32[6]), .sw27(dipswitch_2_sw32[5]),
    .sw28(dipswitch_2_sw32[4]), .sw29(dipswitch_2_sw32[3]), .sw30(dipswitch_2_sw32[2]),
    .sw31(dipswitch_2_sw32[1]), .sw32(dipswitch_2_sw32[0]));
  DipSwitch #(.number(15)) dipswitch_3 (
    .sw1(dipswitch_3_sw15[14]), .sw2(dipswitch_3_sw15[13]), .sw3(dipswitch_3_sw15[12]),
    .sw4(dipswitch_3_sw15[11]), .sw5(dipswitch_3_sw15[10]), .sw6(dipswitch_3_sw15[9]),
    .sw7(dipswitch_3_sw15[8]), .sw8(dipswitch_3_sw15[7]), .sw9(dipswitch_3_sw15[6]),
    .sw10(dipswitch_3_sw15[5]), .sw11(dipswitch_3_sw15[4]), .sw12(dipswitch_3_sw15[3]),
    .sw13(dipswitch_3_sw15[2]), .sw14(dipswitch_3_sw15[1]), .sw15(dipswitch_3_sw15[0]));
  Clock clock_1 (.out(clock_1_out));
  LedBar #(.matrixcols(32)) ledbar_1 (
    .led0(programcounter_1_outp_2[31]), .led1(programcounter_1_outp_2[30]),
    .led2(programcounter_1_outp_2[29]), .led3(programcounter_1_outp_2[28]),
    .led4(programcounter_1_outp_2[27]), .led5(programcounter_1_outp_2[26]),
    .led6(programcounter_1_outp_2[25]), .led7(programcounter_1_outp_2[24]),
    .led8(programcounter_1_outp_2[23]), .led9(programcounter_1_outp_2[22]),
    .led10(programcounter_1_outp_2[21]), .led11(programcounter_1_outp_2[20]),
    .led12(programcounter_1_outp_2[19]), .led13(programcounter_1_outp_2[18]),
    .led14(programcounter_1_outp_2[17]), .led15(programcounter_1_outp[14]),
    .led16(programcounter_1_outp[13]), .led17(programcounter_1_outp[12]), .led18(programcounter_1_outp[11]),
    .led19(programcounter_1_outp[10]), .led20(programcounter_1_outp[9]), .led21(programcounter_1_outp[8]),
    .led22(programcounter_1_outp[7]), .led23(programcounter_1_outp[6]), .led24(programcounter_1_outp[5]),
    .led25(programcounter_1_outp[4]), .led26(programcounter_1_outp[3]), .led27(programcounter_1_outp[2]),
    .led28(programcounter_1_outp[1]), .led29(programcounter_1_outp[0]), .led30(programcounter_1_outp_2[1]),
    .led31(programcounter_1_outp_2[0]));
  ProgramCounter programcounter_1 (
    .Inp(dipswitch_1_sw32), .isBranchTaken(in_1), .clock(clock_1_out),
    .Outp({programcounter_1_outp_2[31:17], programcounter_1_outp, programcounter_1_outp_2[1:0]}));
  LedBar #(.matrixcols(32)) ledbar_2 (
    .led0(ram128kb_1_p6[31]), .led1(ram128kb_1_p6[30]), .led2(ram128kb_1_p6[29]), .led3(ram128kb_1_p6[28]),
    .led4(ram128kb_1_p6[27]), .led5(ram128kb_1_p6[26]), .led6(ram128kb_1_p6[25]), .led7(ram128kb_1_p6[24]),
    .led8(ram128kb_1_p6[23]), .led9(ram128kb_1_p6[22]), .led10(ram128kb_1_p6[21]), .led11(ram128kb_1_p6[20]),
    .led12(ram128kb_1_p6[19]), .led13(ram128kb_1_p6[18]), .led14(ram128kb_1_p6[17]),
    .led15(ram128kb_1_p6[16]), .led16(ram128kb_1_p6[15]), .led17(ram128kb_1_p6[14]),
    .led18(ram128kb_1_p6[13]), .led19(ram128kb_1_p6[12]), .led20(ram128kb_1_p6[11]),
    .led21(ram128kb_1_p6[10]), .led22(ram128kb_1_p6[9]), .led23(ram128kb_1_p6[8]), .led24(ram128kb_1_p6[7]),
    .led25(ram128kb_1_p6[6]), .led26(ram128kb_1_p6[5]), .led27(ram128kb_1_p6[4]), .led28(ram128kb_1_p6[3]),
    .led29(ram128kb_1_p6[2]), .led30(ram128kb_1_p6[1]), .led31(ram128kb_1_p6[0]));
  // Ram128KB ram128kb_1: pin names not known; wires that end beside it: dipswitch_3_sw15, in_2, clock_1_out, dipswitch_2_sw32, programcounter_1_outp, ram128kb_1_p6
endmodule

module ProgramCounter (
  input  [31:0] Inp,
  input  isBranchTaken,
  input  clock,
  output [31:0] Outp
);

  wire adder_1_cout, controlled_buffer_1_out, d_ff_1_q;
  wire [31:0] adder_1_out, multiplexer_1_out;

  Multiplexer #(.width(32)) multiplexer_1 (.in0(adder_1_out), .in1(Inp), .out(multiplexer_1_out), .sel(isBranchTaken));
  D_Flip_Flop d_ff_1 (.D(clock), .clk(clock), .Q(d_ff_1_q));  // open: Qn, preset, reset
  Register #(.width(32)) programCounter (
    .D(multiplexer_1_out), .en(1'b1), .clk(controlled_buffer_1_out), .Q(Outp));  // open: clr
  assign controlled_buffer_1_out = d_ff_1_q ? clock : 1'bz;  // Controlled_Buffer controlled_buffer_1
  Adder #(.width(32)) adder_1 (.a(32'h4), .b(Outp), .out(adder_1_out), .cin(1'b0), .cout(adder_1_cout));
  LED led_1 (.in(adder_1_cout));
endmodule
