// Logisim project InstructionSplitters.circ as structural Verilog: 6 circuits, main circuit R_Splitter
module R_Splitter (
  input  [31:0] instruction,
  output [6:0] opcode,
  output [4:0] rd_i,
  output [2:0] funct_3,
  output [4:0] rs1_i,
  output [4:0] rs2_i,
  output [6:0] funct_7
);


  assign funct_3 = instruction[14:12];
  assign funct_7 = instruction[31:25];
  assign opcode = instruction[6:0];
  assign rd_i = instruction[11:7];
  assign rs1_i = instruction[19:15];
  assign rs2_i = instruction[24:20];
endmodule

module I_Splitter (
  input  [31:0] instruction,
  output [6:0] opcode,
  output [4:0] rd_i,
  output [2:0] funct_3,
  output [4:0] rs1_i,
  output [11:0] immediate
);


  assign funct_3 = instruction[14:12];
  assign immediate = instruction[31:20];
  assign opcode = instruction[6:0];
  assign rd_i = instruction[11:7];
  assign rs1_i = instruction[19:15];
endmodule

module S_Splitter (
  input  [31:0] instruction,
  output [6:0] opcode,
  output [4:0] immediate_4_0,
  output [2:0] funct_3,
  output [4:0] rs1_i,
  output [4:0] rs2_i,
  output [6:0] immediate_11_5
);


  assign funct_3 = instruction[14:12];
  assign immediate_4_0 = instruction[11:7];
  assign immediate_11_5 = instruction[31:25];
  assign opcode = instruction[6:0];
  assign rs1_i = instruction[19:15];
  assign rs2_i = instruction[24:20];
endmodule

module B_Splitter (
  input  [31:0] instruction,
  output [6:0] opcode,
  output immediate_11,
  output [3:0] immediate_4_1,
  output [2:0] funct_3,
  output [4:0] rs1_i,
  output [4:0] rs2_i,
  output [5:0] immediate_10_5,
  output immediate_12
);


  assign funct_3 = instruction[14:12];
  assign immediate_4_1 = instruction[11:8];
  assign immediate_10_5 = instruction[30:25];
  assign immediate_11 = instruction[7];
  assign immediate_12 = instruction[31];
  assign opcode = instruction[6:0];
  assign rs1_i = instruction[19:15];
  assign rs2_i = instruction[24:20];
endmodule

module U_Splitter (
  input  [31:0] instruction,
  output [6:0] opcode,
  output [4:0] rd_i,
  output [19:0] immediate
);


  assign immediate = instruction[31:12];
  assign opcode = instruction[6:0];
  assign rd_i = instruction[11:7];
endmodule

module J_Splitter (
  input  [31:0] instruction,
  output [6:0] opcode,
  output [4:0] rd_i,
  output [7:0] immediate_19_12,
  output immediate_11,
  output [9:0] immediate_10_1,
  output immediate_20
);


  assign immediate_10_1 = instruction[30:21];
  assign immediate_11 = instruction[20];
  assign immediate_19_12 = instruction[19:12];
  assign immediate_20 = instruction[31];
  assign opcode = instruction[6:0];
  assign rd_i = instruction[11:7];
endmodule
