// Logisim project MemoryModule.circ as structural Verilog: 1 circuit, main circuit memoryModule
module memoryModule (
  input  clock,
  input  [31:0] data,
  input  [31:0] address,
  input  [2:0] funct_3,
  output [31:0] memOut
);

  wire comparator_1_gt;
  wire [7:0] multiplexer_2_out, ram128kb_1_outp, ram128kb_1_outp_2, ram128kb_1_outp_3, ram128kb_1_outp_4,
       undriven, undriven_2, undriven_3, undriven_4, undriven_5, undriven_6, undriven_7, undriven_8;
  wire [15:0] multiplexer_3_out;
  wire [31:0] bit_extender_1_out, bit_extender_2_out, bit_extender_3_out, bit_extender_4_out,
       multiplexer_1_out;

  Ram128KB ram128kb_1 (
    .load(comparator_1_gt), .clock(clock), .inp(multiplexer_1_out), .address(address),
    .outp({ram128kb_1_outp_4, ram128kb_1_outp_3, ram128kb_1_outp_2, ram128kb_1_outp}));
  Multiplexer #(.select(3), .width(32)) multiplexer_1 (
    .in5({undriven_4, undriven_3, undriven_2, undriven}),
    .in6({undriven_8, undriven_7, undriven_6, undriven_5}),
    .in7({ram128kb_1_outp_4, ram128kb_1_outp_3, ram128kb_1_outp_2, ram128kb_1_outp}),
    .out(multiplexer_1_out), .sel(funct_3));  // open: in0, in1, in2, in3, in4
  Multiplexer #(.select(2), .width(8)) multiplexer_2 (
    .in0(ram128kb_1_outp), .in1(ram128kb_1_outp_2), .in2(ram128kb_1_outp_3), .in3(ram128kb_1_outp_4),
    .out(multiplexer_2_out), .sel({address[0], address[1]}));
  Multiplexer #(.width(16)) multiplexer_3 (
    .in0({ram128kb_1_outp_2, ram128kb_1_outp}), .in1({ram128kb_1_outp_4, ram128kb_1_outp_3}),
    .out(multiplexer_3_out), .sel(address[1]));
  assign bit_extender_1_out = {{24{multiplexer_2_out[7]}}, multiplexer_2_out};  // Bit_Extender bit_extender_1
  assign bit_extender_2_out = {{24{1'b0}}, multiplexer_2_out};  // Bit_Extender bit_extender_2
  assign bit_extender_3_out = {{16{multiplexer_3_out[15]}}, multiplexer_3_out};  // Bit_Extender bit_extender_3
  assign bit_extender_4_out = {{16{1'b0}}, multiplexer_3_out};  // Bit_Extender bit_extender_4
  Comparator #(.mode("unsigned"), .width(3)) comparator_1 (
    .a(funct_3), .b(3'b100), .gt(comparator_1_gt));  // open: eq, lt
  Multiplexer #(.select(3), .width(32)) multiplexer_4 (
    .in0(bit_extender_1_out), .in1(bit_extender_2_out), .in2(bit_extender_3_out), .in3(bit_extender_4_out),
    .in4({ram128kb_1_outp_4, ram128kb_1_outp_3, ram128kb_1_outp_2, ram128kb_1_outp}), .out(memOut),
    .sel(funct_3));  // open: in5, in6, in7

  // Notes on the sheet:
  //   TODO : @Kepi : modify the signal from the ram using the data and address
  //   halfWord
  //   byte
  //   word
  //   lb
  //   lbu
  //   lh
  //   lhu
  //   lw
endmodule
