// Logisim project Proj_1_ElementaryLogicGates.circ as structural Verilog
module NotGate (
  input  INP,
  output OUTP
);

  nand nand_1 (OUTP, INP, INP);
endmodule

module AndGate (
  input  in_1,
  input  in_2
);

  wire nand_1_out, notgate_1_outp;

  nand nand_1 (nand_1_out, in_1, in_2);
  LED led_1 (.in(notgate_1_outp));
  NotGate notgate_1 (.INP(nand_1_out), .OUTP(notgate_1_outp));
endmodule
