// Logisim project components.circ as structural Verilog: 13 circuits, main circuit Register1
module Register1 (
  input  inp,
  input  in_2,
  input  load,
  output outp
);

  wire multiplexer_1_out;

  Multiplexer multiplexer_1 (.in0(outp), .in1(inp), .out(multiplexer_1_out), .sel(load));
  D_Flip_Flop d_ff_1 (.D(multiplexer_1_out), .clk(in_2), .Q(outp), .preset(1'b0), .reset(1'b0));  // open: Qn
endmodule

module HalfAdder (
  input  a,
  input  b,
  output sum,
  output carry
);

  xor xor_1 (sum, a, b);
  and and_1 (carry, a, b);
endmodule

module FullAdder (
  input  a,
  input  b,
  input  carryIN,
  output carryOUT,
  output sum
);

  wire halfadder_1_carry, halfadder_1_sum, halfadder_2_carry;

  HalfAdder halfadder_1 (.a(a), .b(b), .sum(halfadder_1_sum), .carry(halfadder_1_carry));
  HalfAdder halfadder_2 (.a(halfadder_1_sum), .b(carryIN), .sum(sum), .carry(halfadder_2_carry));
  or or_1 (carryOUT, halfadder_1_carry, halfadder_2_carry);
endmodule

module Adder32 (
  input  [31:0] a,
  input  [31:0] b,
  output [31:0] c
);

  wire fulladder_1_carryout, fulladder_2_carryout, fulladder_3_carryout, fulladder_4_carryout,
       fulladder_5_carryout, fulladder_6_carryout, fulladder_7_carryout, fulladder_8_carryout,
       fulladder_9_carryout, fulladder_10_carryout, fulladder_11_carryout, fulladder_12_carryout,
       fulladder_13_carryout, fulladder_14_carryout, fulladder_15_carryout, fulladder_16_carryout,
       fulladder_17_carryout, fulladder_18_carryout, fulladder_19_carryout, fulladder_20_carryout,
       fulladder_21_carryout, fulladder_22_carryout, fulladder_23_carryout, fulladder_24_carryout,
       fulladder_25_carryout, fulladder_26_carryout, fulladder_27_carryout, fulladder_28_carryout,
       fulladder_29_carryout, fulladder_30_carryout, fulladder_31_carryout;

  FullAdder fulladder_1 (.a(a[0]), .b(b[0]), .carryIN(1'b0), .carryOUT(fulladder_1_carryout), .sum(c[0]));
  FullAdder fulladder_2 (
    .a(a[1]), .b(b[1]), .carryIN(fulladder_1_carryout), .carryOUT(fulladder_2_carryout), .sum(c[1]));
  FullAdder fulladder_3 (
    .a(a[2]), .b(b[2]), .carryIN(fulladder_2_carryout), .carryOUT(fulladder_3_carryout), .sum(c[2]));
  FullAdder fulladder_4 (
    .a(a[3]), .b(b[3]), .carryIN(fulladder_3_carryout), .carryOUT(fulladder_4_carryout), .sum(c[3]));
  FullAdder fulladder_5 (
    .a(a[4]), .b(b[4]), .carryIN(fulladder_4_carryout), .carryOUT(fulladder_5_carryout), .sum(c[4]));
  FullAdder fulladder_6 (
    .a(a[5]), .b(b[5]), .carryIN(fulladder_5_carryout), .carryOUT(fulladder_6_carryout), .sum(c[5]));
  FullAdder fulladder_7 (
    .a(a[6]), .b(b[6]), .carryIN(fulladder_6_carryout), .carryOUT(fulladder_7_carryout), .sum(c[6]));
  FullAdder fulladder_8 (
    .a(a[7]), .b(b[7]), .carryIN(fulladder_7_carryout), .carryOUT(fulladder_8_carryout), .sum(c[7]));
  FullAdder fulladder_9 (
    .a(a[8]), .b(b[8]), .carryIN(fulladder_8_carryout), .carryOUT(fulladder_9_carryout), .sum(c[8]));
  FullAdder fulladder_10 (
    .a(a[9]), .b(b[9]), .carryIN(fulladder_9_carryout), .carryOUT(fulladder_10_carryout), .sum(c[9]));
  FullAdder fulladder_11 (
    .a(a[10]), .b(b[10]), .carryIN(fulladder_10_carryout), .carryOUT(fulladder_11_carryout), .sum(c[10]));
  FullAdder fulladder_12 (
    .a(a[11]), .b(b[11]), .carryIN(fulladder_11_carryout), .carryOUT(fulladder_12_carryout), .sum(c[11]));
  FullAdder fulladder_13 (
    .a(a[12]), .b(b[12]), .carryIN(fulladder_12_carryout), .carryOUT(fulladder_13_carryout), .sum(c[12]));
  FullAdder fulladder_14 (
    .a(a[13]), .b(b[13]), .carryIN(fulladder_13_carryout), .carryOUT(fulladder_14_carryout), .sum(c[13]));
  FullAdder fulladder_15 (
    .a(a[14]), .b(b[14]), .carryIN(fulladder_14_carryout), .carryOUT(fulladder_15_carryout), .sum(c[14]));
  FullAdder fulladder_16 (
    .a(a[15]), .b(b[15]), .carryIN(fulladder_15_carryout), .carryOUT(fulladder_16_carryout), .sum(c[15]));
  FullAdder fulladder_17 (
    .a(a[16]), .b(b[16]), .carryIN(fulladder_16_carryout), .carryOUT(fulladder_17_carryout), .sum(c[16]));
  FullAdder fulladder_18 (
    .a(a[17]), .b(b[17]), .carryIN(fulladder_17_carryout), .carryOUT(fulladder_18_carryout), .sum(c[17]));
  FullAdder fulladder_19 (
    .a(a[18]), .b(b[18]), .carryIN(fulladder_18_carryout), .carryOUT(fulladder_19_carryout), .sum(c[18]));
  FullAdder fulladder_20 (
    .a(a[19]), .b(b[19]), .carryIN(fulladder_19_carryout), .carryOUT(fulladder_20_carryout), .sum(c[19]));
  FullAdder fulladder_21 (
    .a(a[20]), .b(b[20]), .carryIN(fulladder_20_carryout), .carryOUT(fulladder_21_carryout), .sum(c[20]));
  FullAdder fulladder_22 (
    .a(a[21]), .b(b[21]), .carryIN(fulladder_21_carryout), .carryOUT(fulladder_22_carryout), .sum(c[21]));
  FullAdder fulladder_23 (
    .a(a[22]), .b(b[22]), .carryIN(fulladder_22_carryout), .carryOUT(fulladder_23_carryout), .sum(c[22]));
  FullAdder fulladder_24 (
    .a(a[23]), .b(b[23]), .carryIN(fulladder_23_carryout), .carryOUT(fulladder_24_carryout), .sum(c[23]));
  FullAdder fulladder_25 (
    .a(a[24]), .b(b[24]), .carryIN(fulladder_24_carryout), .carryOUT(fulladder_25_carryout), .sum(c[24]));
  FullAdder fulladder_26 (
    .a(a[25]), .b(b[25]), .carryIN(fulladder_25_carryout), .carryOUT(fulladder_26_carryout), .sum(c[25]));
  FullAdder fulladder_27 (
    .a(a[26]), .b(b[26]), .carryIN(fulladder_26_carryout), .carryOUT(fulladder_27_carryout), .sum(c[26]));
  FullAdder fulladder_28 (
    .a(a[27]), .b(b[27]), .carryIN(fulladder_27_carryout), .carryOUT(fulladder_28_carryout), .sum(c[27]));
  FullAdder fulladder_29 (
    .a(a[28]), .b(b[28]), .carryIN(fulladder_28_carryout), .carryOUT(fulladder_29_carryout), .sum(c[28]));
  FullAdder fulladder_30 (
    .a(a[29]), .b(b[29]), .carryIN(fulladder_29_carryout), .carryOUT(fulladder_30_carryout), .sum(c[29]));
  FullAdder fulladder_31 (
    .a(a[30]), .b(b[30]), .carryIN(fulladder_30_carryout), .carryOUT(fulladder_31_carryout), .sum(c[30]));
  FullAdder fulladder_32 (.a(a[31]), .b(b[31]), .carryIN(fulladder_31_carryout), .sum(c[31]));  // open: carryOUT
endmodule

module Increment32 (
  input  [31:0] in_1,
  output [31:0] out_2
);

  Adder32 adder32_1 (.a(in_1), .b(32'h1), .c(out_2));
endmodule

module Register2 (
  input  [1:0] inp,
  input  clock,
  input  load,
  output [1:0] outp
);

  Register1 register1_1 (.inp(inp[0]), .in_2(clock), .load(load), .outp(outp[0]));
  Register1 register1_2 (.inp(inp[1]), .in_2(clock), .load(load), .outp(outp[1]));
endmodule

module Register4 (
  input  [3:0] inp,
  input  clock,
  input  load,
  output [3:0] outp
);

  Register2 register2_1 (.inp(inp[1:0]), .clock(clock), .outp(outp[1:0]), .load(load));
  Register2 register2_2 (.inp(inp[3:2]), .clock(clock), .outp(outp[3:2]), .load(load));
endmodule

module Register8 (
  input  [7:0] inp,
  input  clock,
  input  load,
  output [7:0] outp
);

  Register4 register4_1 (.inp(inp[3:0]), .clock(clock), .load(load), .outp(outp[3:0]));
  Register4 register4_2 (.inp(inp[7:4]), .clock(clock), .load(load), .outp(outp[7:4]));
endmodule

module Register16 (
  input  [15:0] inp,
  input  clock,
  input  load,
  output [15:0] outp
);

  Register8 register8_1 (.inp(inp[7:0]), .clock(clock), .load(load), .outp(outp[7:0]));
  Register8 register8_2 (.inp(inp[15:8]), .clock(clock), .load(load), .outp(outp[15:8]));
endmodule

module Register32 (
  input  [31:0] inp,
  input  clock,
  input  load,
  output [31:0] outp
);

  Register16 register16_1 (.inp(inp[15:0]), .clock(clock), .load(load), .outp(outp[15:0]));
  Register16 register16_2 (.inp(inp[31:16]), .clock(clock), .load(load), .outp(outp[31:16]));
endmodule

module Ram32x8 (
  input  load,
  input  [31:0] inp,
  input  clock,
  input  [2:0] address,
  output [31:0] outp
);

  wire demultiplexer_1_out0, demultiplexer_1_out1, demultiplexer_1_out2, demultiplexer_1_out3,
       demultiplexer_1_out4, demultiplexer_1_out5, demultiplexer_1_out6, demultiplexer_1_out7;
  wire [31:0] register32_1_outp, register32_2_outp, register32_3_outp, register32_4_outp, register32_5_outp,
       register32_6_outp, register32_7_outp, register32_8_outp;

  Demultiplexer #(.select(3)) demultiplexer_1 (
    .out0(demultiplexer_1_out0), .out1(demultiplexer_1_out1), .out2(demultiplexer_1_out2),
    .out3(demultiplexer_1_out3), .out4(demultiplexer_1_out4), .out5(demultiplexer_1_out5),
    .out6(demultiplexer_1_out6), .out7(demultiplexer_1_out7), .in(load), .sel(address));
  Register32 register32_1 (.inp(inp), .clock(clock), .load(demultiplexer_1_out0), .outp(register32_1_outp));
  Register32 register32_2 (.inp(inp), .clock(clock), .load(demultiplexer_1_out1), .outp(register32_2_outp));
  Register32 register32_3 (.inp(inp), .clock(clock), .load(demultiplexer_1_out2), .outp(register32_3_outp));
  Register32 register32_4 (.inp(inp), .clock(clock), .load(demultiplexer_1_out3), .outp(register32_4_outp));
  Register32 register32_5 (.inp(inp), .clock(clock), .load(demultiplexer_1_out4), .outp(register32_5_outp));
  Register32 register32_6 (.inp(inp), .clock(clock), .load(demultiplexer_1_out5), .outp(register32_6_outp));
  Register32 register32_7 (.inp(inp), .clock(clock), .load(demultiplexer_1_out6), .outp(register32_7_outp));
  Register32 register32_8 (.inp(inp), .clock(clock), .load(demultiplexer_1_out7), .outp(register32_8_outp));
  Multiplexer #(.select(3), .width(32)) multiplexer_1 (
    .in0(register32_1_outp), .in1(register32_2_outp), .in2(register32_3_outp), .in3(register32_4_outp),
    .in4(register32_5_outp), .in5(register32_6_outp), .in6(register32_7_outp), .in7(register32_8_outp),
    .out(outp), .sel(address));
endmodule

module test (
  input  in_1,
  input  in_2
);

  wire clock_1_out, clock_2_out;
  wire [31:0] dipswitch_1_sw32, dipswitch_2_sw32, dipswitch_3_sw32, ram128kb_1_outp;

  DipSwitch #(.number(32)) dipswitch_1 (
    .sw1(dipswitch_1_sw32[31]), .sw2(dipswitch_1_sw32[30]), .sw3(dipswitch_1_sw32[29]),
    .sw4(dipswitch_1_sw32[28]), .sw5(dipswitch_1_sw32[27]), .sw6(dipswitch_1_sw32[26]),
    .sw7(dipswitch_1_sw32[25]), .sw8(dipswitch_1_sw32[24]), .sw9(dipswitch_1_sw32[23]),
    .sw10(dipswitch_1_sw32[22]), .sw11(dipswitch_1_sw32[21]), .sw12(dipswitch_1_sw32[20]),
    .sw13(dipswitch_1_sw32[19]), .sw14(dipswitch_1_sw32[18]), .sw15(dipswitch_1_sw32[17]),
    .sw16(dipswitch_1_sw32[16]), .sw17(dipswitch_1_sw32[15]), .sw18(dipswitch_1_sw32[14]),
    .sw19(dipswitch_1_sw32[13]), .sw20(dipswitch_1_sw32[12]), .sw21(dipswitch_1_sw32[11]),
    .sw22(dipswitch_1_sw32[10]), .sw23(dipswitch_1_sw32[9]), .sw24(dipswitch_1_sw32[8]),
    .sw25(dipswitch_1_sw32[7]), .sw26(dipswitch_1_sw32[6]), .sw27(dipswitch_1_sw32[5]),
    .sw28(dipswitch_1_sw32[4]), .sw29(dipswitch_1_sw32[3]), .sw30(dipswitch_1_sw32[2]),
    .sw31(dipswitch_1_sw32[1]), .sw32(dipswitch_1_sw32[0]));
  DipSwitch #(.number(32)) dipswitch_2 (
    .sw1(dipswitch_2_sw32[31]), .sw2(dipswitch_2_sw32[30]), .sw3(dipswitch_2_sw32[29]),
    .sw4(dipswitch_2_sw32[28]), .sw5(dipswitch_2_sw32[27]), .sw6(dipswitch_2_sw32[26]),
    .sw7(dipswitch_2_sw32[25]), .sw8(dipswitch_2_sw32[24]), .sw9(dipswitch_2_sw32[23]),
    .sw10(dipswitch_2_sw32[22]), .sw11(dipswitch_2_sw32[21]), .sw12(dipswitch_2_sw32[20]),
    .sw13(dipswitch_2_sw32[19]), .sw14(dipswitch_2_sw32[18]), .sw15(dipswitch_2_sw32[17]),
    .sw16(dipswitch_2_sw32[16]), .sw17(dipswitch_2_sw32[15]), .sw18(dipswitch_2_sw32[14]),
    .sw19(dipswitch_2_sw32[13]), .sw20(dipswitch_2_sw32[12]), .sw21(dipswitch_2_sw32[11]),
    .sw22(dipswitch_2_sw32[10]), .sw23(dipswitch_2_sw32[9]), .sw24(dipswitch_2_sw32[8]),
    .sw25(dipswitch_2_sw32[7]), .sw26(dipswitch_2_sw32[6]), .sw27(dipswitch_2_sw32[5]),
    .sw28(dipswitch_2_sw32[4]), .sw29(dipswitch_2_sw32[3]), .sw30(dipswitch_2_sw32[2]),
    .sw31(dipswitch_2_sw32[1]), .sw32(dipswitch_2_sw32[0]));
  DipSwitch #(.number(32)) dipswitch_3 (
    .sw1(dipswitch_3_sw32[31]), .sw2(dipswitch_3_sw32[30]), .sw3(dipswitch_3_sw32[29]),
    .sw4(dipswitch_3_sw32[28]), .sw5(dipswitch_3_sw32[27]), .sw6(dipswitch_3_sw32[26]),
    .sw7(dipswitch_3_sw32[25]), .sw8(dipswitch_3_sw32[24]), .sw9(dipswitch_3_sw32[23]),
    .sw10(dipswitch_3_sw32[22]), .sw11(dipswitch_3_sw32[21]), .sw12(dipswitch_3_sw32[20]),
    .sw13(dipswitch_3_sw32[19]), .sw14(dipswitch_3_sw32[18]), .sw15(dipswitch_3_sw32[17]),
    .sw16(dipswitch_3_sw32[16]), .sw17(dipswitch_3_sw32[15]), .sw18(dipswitch_3_sw32[14]),
    .sw19(dipswitch_3_sw32[13]), .sw20(dipswitch_3_sw32[12]), .sw21(dipswitch_3_sw32[11]),
    .sw22(dipswitch_3_sw32[10]), .sw23(dipswitch_3_sw32[9]), .sw24(dipswitch_3_sw32[8]),
    .sw25(dipswitch_3_sw32[7]), .sw26(dipswitch_3_sw32[6]), .sw27(dipswitch_3_sw32[5]),
    .sw28(dipswitch_3_sw32[4]), .sw29(dipswitch_3_sw32[3]), .sw30(dipswitch_3_sw32[2]),
    .sw31(dipswitch_3_sw32[1]), .sw32(dipswitch_3_sw32[0]));
  Clock clock_1 (.out(clock_1_out));
  Clock clock_2 (.out(clock_2_out));
  LedBar #(.matrixcols(32)) ledbar_1 (
    .led0(ram128kb_1_outp[31]), .led1(ram128kb_1_outp[30]), .led2(ram128kb_1_outp[29]),
    .led3(ram128kb_1_outp[28]), .led4(ram128kb_1_outp[27]), .led5(ram128kb_1_outp[26]),
    .led6(ram128kb_1_outp[25]), .led7(ram128kb_1_outp[24]), .led8(ram128kb_1_outp[23]),
    .led9(ram128kb_1_outp[22]), .led10(ram128kb_1_outp[21]), .led11(ram128kb_1_outp[20]),
    .led12(ram128kb_1_outp[19]), .led13(ram128kb_1_outp[18]), .led14(ram128kb_1_outp[17]),
    .led15(ram128kb_1_outp[16]), .led16(ram128kb_1_outp[15]), .led17(ram128kb_1_outp[14]),
    .led18(ram128kb_1_outp[13]), .led19(ram128kb_1_outp[12]), .led20(ram128kb_1_outp[11]),
    .led21(ram128kb_1_outp[10]), .led22(ram128kb_1_outp[9]), .led23(ram128kb_1_outp[8]),
    .led24(ram128kb_1_outp[7]), .led25(ram128kb_1_outp[6]), .led26(ram128kb_1_outp[5]),
    .led27(ram128kb_1_outp[4]), .led28(ram128kb_1_outp[3]), .led29(ram128kb_1_outp[2]),
    .led30(ram128kb_1_outp[1]), .led31(ram128kb_1_outp[0]));
  Ram128KB ram128kb_1 (
    .load(in_1), .clock(clock_1_out), .inp(dipswitch_1_sw32), .address(dipswitch_2_sw32[14:0]),
    .outp(ram128kb_1_outp));
  Ram32x8 ram32x8_1 (.load(in_2), .inp(dipswitch_3_sw32), .clock(clock_2_out));  // open: address, outp
  // Pins of 15 and 32 bits meet at dipswitch_2_sw32
endmodule

module Ram128KB (
  input  load,
  input  clock,
  input  [31:0] inp,
  input  [14:0] address,
  output [31:0] outp
);

  RAM #(.addrWidth(15), .dataWidth(32)) ram_1 (
    .addr(address), .we(load), .oe(1'b1), .clk(clock), .din(inp), .dout(outp));
endmodule
